# Fritzing sketch Wiring_Fritzing (saved by Fritzing 0.9.3b)
circuit board: 8.50048cm x 5cm
breadboards: 1

parts:
  DFRobot_DFPlayer_Mini1 = DFRobot DFPlayer Mini [part_number=DFR0299]
  Light_sensor = PHOTOCELL [package=photocell-kit]
  WS2812b = female pin header, 3 pins [form="♀ (female)"]
  Speaker = female pin header, 4 pins [form="♀ (female)"]
  LED = female pin header, 4 pins [form="♀ (female)"]
  RotEnc = female pin header, 5 pins [form="♀ (female)"]
  220Ω = Resistor [tolerance=±5% resistance=220 package=THT]
  330Ω = Resistor [tolerance=±5% resistance=330 package=THT]
  1kΩ = Resistor [tolerance=±5% resistance=1k package=THT]
  RTC = female pin header, 6 pins [form="♀ (female)"]
  ESP32_D1_Mini = MH-ET Live ESP32 Mini Kit
  Switch = female pin header, 3 pins [form="♀ (female)"]

nets:
  N1: DFRobot_DFPlayer_Mini1.VCC, WS2812b.pin3, LED.pin2, ESP32_D1_Mini.connector28
  N2: DFRobot_DFPlayer_Mini1.RX, 220Ω.Pin_0
  N3: DFRobot_DFPlayer_Mini1.TX, ESP32_D1_Mini.connector26
  N4: DFRobot_DFPlayer_Mini1.SPK_1, Speaker.pin1, Speaker.pin2
  N5: DFRobot_DFPlayer_Mini1.GND-1, DFRobot_DFPlayer_Mini1.GND-2, WS2812b.pin1, LED.pin1, RotEnc.pin1, 1kΩ.Pin_1, RTC.pin2, ESP32_D1_Mini.connector1, ESP32_D1_Mini.connector27
  N6: DFRobot_DFPlayer_Mini1.SPK_2, Speaker.pin3, Speaker.pin4
  N7: Light_sensor.P$1, RotEnc.pin2, RTC.pin3, ESP32_D1_Mini.connector18, Switch.pin1
  N8: Light_sensor.P$2, 1kΩ.Pin_0, ESP32_D1_Mini.connector12
  N9: WS2812b.pin2, 330Ω.Pin_0
  N10: LED.pin3, ESP32_D1_Mini.connector15
  N11: LED.pin4, ESP32_D1_Mini.connector14
  N12: RotEnc.pin3, ESP32_D1_Mini.connector29
  N13: RotEnc.pin4, ESP32_D1_Mini.connector34
  N14: RotEnc.pin5, ESP32_D1_Mini.connector33
  N15: 220Ω.Pin_1, ESP32_D1_Mini.connector25
  N16: 330Ω.Pin_1, ESP32_D1_Mini.connector32
  N17: RTC.pin4, ESP32_D1_Mini.connector24
  N18: RTC.pin5, ESP32_D1_Mini.connector23
  N19: ESP32_D1_Mini.connector36, Switch.pin2
  N20: ESP32_D1_Mini.connector37, Switch.pin3

notes:
  OGrünig
  2021
  v0.5
